// Logisim project mico_x1.circ as structural Verilog: 10 circuits, main circuit Mico_X1
module Mico_X1 (
);

  wire and_1_out, BRWE, CLK, CTE, DWE, multiplexer_2_out, zero;
  wire [1:0] JMP, Memoria_de_controle_data;
  wire [2:0] sULA;
  wire [3:0] Memoria_de_programa_data, Memoria_de_programa_data_2, Memoria_de_programa_data_3,
       Memoria_de_programa_data_4, Memoria_de_programa_data_5, Memoria_de_programa_data_6,
       Memoria_de_programa_data_7, Memoria_de_programa_data_8;
  wire [31:0] banco_de_registradores_16x32b_1_outa, banco_de_registradores_16x32b_1_outb, bit_extender_1_out,
       bit_extender_2_out, carrylookahead_adder_32b_1_s, IP_q, multiplexer_1_p4, multiplexer_4_out, ula_1_s;

  assign bit_extender_1_out = {{16{Memoria_de_programa_data_4[3]}}, {Memoria_de_programa_data_4, Memoria_de_programa_data_3, Memoria_de_programa_data_2, Memoria_de_programa_data}};  // Bit_Extender bit_extender_1
  Clock clock_1 (.out(CLK));
  // Multiplexer #(.select(2), .width(32)) multiplexer_1: pin names not known; wires that end beside it: 32'h1, bit_extender_1_out, {32{1'b0}}, multiplexer_1_p4, JMP
  Multiplexer #(.select(2)) multiplexer_2 (
    .in0(1'b0), .in1(bit_extender_1_out[31]), .in2(1'b0), .out(multiplexer_2_out));  // open: in3, sel
  CarryLookAhead_adder_32b carrylookahead_adder_32b_1 (
    .A(IP_q), .B(multiplexer_1_p4), .Cin(multiplexer_2_out), .S(carrylookahead_adder_32b_1_s));
  Register #(.width(32)) IP (.D(carrylookahead_adder_32b_1_s), .en(1'b1), .clk(CLK), .Q(IP_q));  // open: clr
  ROM #(.addrWidth(24), .dataWidth(32)) Memoria_de_programa (
    .addr(IP_q[23:0]),
    .data({Memoria_de_programa_data_8, Memoria_de_programa_data_7, Memoria_de_programa_data_6, Memoria_de_programa_data_5, Memoria_de_programa_data_4, Memoria_de_programa_data_3, Memoria_de_programa_data_2, Memoria_de_programa_data}));
  ROM #(.addrWidth(4)) Memoria_de_controle (
    .addr(Memoria_de_programa_data_8), .data({sULA, Memoria_de_controle_data, CTE, BRWE, DWE}));
  Banco_de_Registradores_16x32b banco_de_registradores_16x32b_1 (
    .endA(Memoria_de_programa_data_7), .endB(Memoria_de_programa_data_6), .dataC(ula_1_s),
    .endC(Memoria_de_programa_data_5), .WE(BRWE), .CLK(CLK), .outA(banco_de_registradores_16x32b_1_outa),
    .outB(banco_de_registradores_16x32b_1_outb));
  assign bit_extender_2_out = {{16{1'b0}}, {Memoria_de_programa_data_4, Memoria_de_programa_data_3, Memoria_de_programa_data_2, Memoria_de_programa_data}};  // Bit_Extender bit_extender_2
  and and_1 (and_1_out, sULA[0], zero);
  Multiplexer #(.width(2)) multiplexer_3 (.in0(Memoria_de_controle_data), .in1(2'b00), .out(JMP));  // open: sel
  Multiplexer #(.width(32)) multiplexer_4 (
    .in0(banco_de_registradores_16x32b_1_outb), .in1(bit_extender_2_out), .out(multiplexer_4_out), .sel(CTE));
  Register #(.width(32)) display (.D(banco_de_registradores_16x32b_1_outa), .en(DWE), .clk(CLK));  // open: Q, clr
  ULA ula_1 (.A(banco_de_registradores_16x32b_1_outa), .B(multiplexer_4_out), .seletor(sULA), .S(ula_1_s), .zero(zero));
endmodule

module ULA (
  input  [31:0] A,
  input  [2:0] seletor,
  input  [31:0] B,
  output zero,
  output [31:0] S
);

  wire [31:0] and_1_out, Lshift_s, not_1_out, not_2_out, or_1_out, Rshift_s, soma_s, subtracao_s, xor_1_out;

  CarryLookAhead_adder_32b soma (.A(A), .B(B), .Cin(1'b0), .S(soma_s));
  CarryLookAhead_adder_32b subtracao (.A(A), .B(not_1_out), .Cin(1'b1), .S(subtracao_s));
  assign not_1_out = ~B;  // NOT_Gate not_1, 32 bits wide
  Left_Shifter_32b Lshift (.B(B), .A(A), .S(Lshift_s));
  Right_Shifter_32b Rshift (.B(B), .A(A), .S(Rshift_s));
  assign and_1_out = A & B;  // AND_Gate and_1, 32 bits wide
  assign or_1_out = A | B;  // OR_Gate or_1, 32 bits wide
  assign xor_1_out = A ^ B;  // XOR_Gate xor_1, 32 bits wide
  assign not_2_out = ~A;  // NOT_Gate not_2, 32 bits wide
  Multiplexer #(.select(3), .width(32)) multiplexer_1 (
    .in0(soma_s), .in1(subtracao_s), .in2(and_1_out), .in3(or_1_out), .in4(xor_1_out), .in5(not_2_out),
    .in6(Lshift_s), .in7(Rshift_s), .out(S), .sel(seletor));
  nor nor_1 (zero, S[0], S[1], S[2], S[3], S[4], S[5], S[6], S[7], S[8], S[9], S[10], S[11], S[12], S[13], S[14], S[15], S[17], S[18], S[19], S[20], S[21], S[22], S[23], S[24], S[25], S[26], S[27], S[28], S[29], S[30], S[31], S[16]);
endmodule

// BancoReg16x32b
module Banco_de_Registradores_16x32b (
  input  WE,
  input  [3:0] endA,
  input  [31:0] dataC,
  input  [3:0] endC,
  input  [3:0] endB,
  input  CLK,
  output [31:0] outA,
  output [31:0] outB
);

  wire [31:0] demultiplexer_1_out0, demultiplexer_1_out1, demultiplexer_1_out2, demultiplexer_1_out3,
       demultiplexer_1_out4, demultiplexer_1_out5, demultiplexer_1_out6, demultiplexer_1_out7,
       demultiplexer_1_out8, demultiplexer_1_out9, demultiplexer_1_out10, demultiplexer_1_out11,
       demultiplexer_1_out12, demultiplexer_1_out13, demultiplexer_1_out14, demultiplexer_1_out15, r0, r1,
       r2, r3, r4, r5, r6, r7, r8, r9, r10, r11, r12, r13, r14, r15;

  Demultiplexer #(.select(4), .width(32)) demultiplexer_1 (
    .out0(demultiplexer_1_out0), .out1(demultiplexer_1_out1), .out2(demultiplexer_1_out2),
    .out3(demultiplexer_1_out3), .out4(demultiplexer_1_out4), .out5(demultiplexer_1_out5),
    .out6(demultiplexer_1_out6), .out7(demultiplexer_1_out7), .out8(demultiplexer_1_out8),
    .out9(demultiplexer_1_out9), .out10(demultiplexer_1_out10), .out11(demultiplexer_1_out11),
    .out12(demultiplexer_1_out12), .out13(demultiplexer_1_out13), .out14(demultiplexer_1_out14),
    .out15(demultiplexer_1_out15), .in(dataC), .sel(endC));
  Register #(.width(32)) register_1 (.D(demultiplexer_1_out0), .en(WE), .clk(CLK), .Q(r0), .clr(1'b1));
  Register #(.width(32)) register_2 (.D(demultiplexer_1_out4), .en(WE), .clk(CLK), .Q(r4));  // open: clr
  Register #(.width(32)) register_3 (.D(demultiplexer_1_out11), .en(WE), .clk(CLK), .Q(r11));  // open: clr
  Register #(.width(32)) register_4 (.D(demultiplexer_1_out15), .en(WE), .clk(CLK), .Q(r15));  // open: clr
  Register #(.width(32)) register_5 (.D(demultiplexer_1_out1), .en(WE), .clk(CLK), .Q(r1));  // open: clr
  Register #(.width(32)) register_6 (.D(demultiplexer_1_out5), .en(WE), .clk(CLK), .Q(r5));  // open: clr
  Register #(.width(32)) register_7 (.D(demultiplexer_1_out10), .en(WE), .clk(CLK), .Q(r10));  // open: clr
  Register #(.width(32)) register_8 (.D(demultiplexer_1_out14), .en(WE), .clk(CLK), .Q(r14));  // open: clr
  Register #(.width(32)) register_9 (.D(demultiplexer_1_out2), .en(WE), .clk(CLK), .Q(r2));  // open: clr
  Register #(.width(32)) register_10 (.D(demultiplexer_1_out6), .en(WE), .clk(CLK), .Q(r6));  // open: clr
  Register #(.width(32)) register_11 (.D(demultiplexer_1_out9), .en(WE), .clk(CLK), .Q(r9));  // open: clr
  Register #(.width(32)) register_12 (.D(demultiplexer_1_out13), .en(WE), .clk(CLK), .Q(r13));  // open: clr
  Register #(.width(32)) register_13 (.D(demultiplexer_1_out3), .en(WE), .clk(CLK), .Q(r3));  // open: clr
  Register #(.width(32)) register_14 (.D(demultiplexer_1_out7), .en(WE), .clk(CLK), .Q(r7));  // open: clr
  Register #(.width(32)) register_15 (.D(demultiplexer_1_out8), .en(WE), .clk(CLK), .Q(r8));  // open: clr
  Register #(.width(32)) register_16 (.D(demultiplexer_1_out12), .en(WE), .clk(CLK), .Q(r12));  // open: clr
  Multiplexer #(.select(4), .width(32)) multiplexer_1 (
    .in0(r0), .in1(r1), .in2(r2), .in3(r3), .in4(r4), .in5(r5), .in6(r6), .in7(r7), .in8(r8), .in9(r9),
    .in10(r10), .in11(r11), .in12(r12), .in13(r13), .in14(r14), .in15(r15), .out(outA), .sel(endA));
  Multiplexer #(.select(4), .width(32)) multiplexer_2 (
    .in0(r0), .in1(r1), .in2(r2), .in3(r3), .in4(r4), .in5(r5), .in6(r6), .in7(r7), .in8(r8), .in9(r9),
    .in10(r10), .in11(r11), .in12(r12), .in13(r13), .in14(r14), .in15(r15), .out(outB), .sel(endB));
endmodule

// ZeroExt
module Unsigned_Extension_16_32 (
  input  [15:0] E,
  output [31:0] S
);


  assign S = {{16{1'b0}}, E};
endmodule

// SignExt
module Signed_Extension_16_32 (
  input  [15:0] E,
  output [31:0] S
);


  assign S = {{17{E[15]}}, E[14:0]};
endmodule

// CLAadder32b
module CarryLookAhead_adder_32b (
  input  [31:0] B,
  input  Cin,
  input  [31:0] A,
  output [31:0] S
);

  wire carrylookahead_logic_4b_1_c1, carrylookahead_logic_4b_1_c2, carrylookahead_logic_4b_1_c3,
       carrylookahead_logic_4b_2_c1, carrylookahead_logic_4b_2_c2, carrylookahead_logic_4b_2_c3,
       carrylookahead_logic_4b_2_c4, carrylookahead_logic_4b_3_c1, carrylookahead_logic_4b_3_c2,
       carrylookahead_logic_4b_3_c3, carrylookahead_logic_4b_3_c4, carrylookahead_logic_4b_4_c1,
       carrylookahead_logic_4b_4_c2, carrylookahead_logic_4b_4_c3, carrylookahead_logic_4b_4_c4,
       carrylookahead_logic_4b_5_c1, carrylookahead_logic_4b_5_c2, carrylookahead_logic_4b_5_c3,
       carrylookahead_logic_4b_5_c4, carrylookahead_logic_4b_6_c1, carrylookahead_logic_4b_6_c2,
       carrylookahead_logic_4b_6_c3, carrylookahead_logic_4b_6_c4, carrylookahead_logic_4b_7_c1,
       carrylookahead_logic_4b_7_c2, carrylookahead_logic_4b_7_c3, carrylookahead_logic_4b_7_c4,
       carrylookahead_logic_4b_8_c1, carrylookahead_logic_4b_8_c2, carrylookahead_logic_4b_8_c3,
       carrylookahead_logic_4b_8_c4;

  Full_Adder full_adder_1 (.A(A[31]), .B(B[31]), .Cin(carrylookahead_logic_4b_1_c3), .S(S[31]));  // open: Cout
  CarryLookAhead_logic_4b carrylookahead_logic_4b_1 (
    .A3(A[31]), .B3(B[31]), .A2(A[30]), .B2(B[30]), .A1(A[29]), .B1(B[29]), .A0(A[28]), .B0(B[28]),
    .Cin(carrylookahead_logic_4b_2_c4), .C3(carrylookahead_logic_4b_1_c3), .C2(carrylookahead_logic_4b_1_c2),
    .C1(carrylookahead_logic_4b_1_c1));  // open: C4
  Full_Adder full_adder_2 (.A(A[30]), .B(B[30]), .Cin(carrylookahead_logic_4b_1_c2), .S(S[30]));  // open: Cout
  Full_Adder full_adder_3 (.A(A[29]), .B(B[29]), .Cin(carrylookahead_logic_4b_1_c1), .S(S[29]));  // open: Cout
  Full_Adder full_adder_4 (.A(A[28]), .B(B[28]), .Cin(carrylookahead_logic_4b_2_c4), .S(S[28]));  // open: Cout
  Full_Adder full_adder_5 (.A(A[27]), .B(B[27]), .Cin(carrylookahead_logic_4b_2_c3), .S(S[27]));  // open: Cout
  CarryLookAhead_logic_4b carrylookahead_logic_4b_2 (
    .A3(A[27]), .B3(B[27]), .A2(A[26]), .B2(B[26]), .A1(A[25]), .B1(B[25]), .A0(A[24]), .B0(B[24]),
    .Cin(carrylookahead_logic_4b_3_c4), .C4(carrylookahead_logic_4b_2_c4), .C3(carrylookahead_logic_4b_2_c3),
    .C2(carrylookahead_logic_4b_2_c2), .C1(carrylookahead_logic_4b_2_c1));
  Full_Adder full_adder_6 (.A(A[26]), .B(B[26]), .Cin(carrylookahead_logic_4b_2_c2), .S(S[26]));  // open: Cout
  Full_Adder full_adder_7 (.A(A[25]), .B(B[25]), .Cin(carrylookahead_logic_4b_2_c1), .S(S[25]));  // open: Cout
  Full_Adder full_adder_8 (.A(A[24]), .B(B[24]), .Cin(carrylookahead_logic_4b_3_c4), .S(S[24]));  // open: Cout
  Full_Adder full_adder_9 (.A(A[23]), .B(B[23]), .Cin(carrylookahead_logic_4b_3_c3), .S(S[23]));  // open: Cout
  CarryLookAhead_logic_4b carrylookahead_logic_4b_3 (
    .A3(A[23]), .B3(B[23]), .A2(A[22]), .B2(B[22]), .A1(A[21]), .B1(B[21]), .A0(A[20]), .B0(B[20]),
    .Cin(carrylookahead_logic_4b_4_c4), .C4(carrylookahead_logic_4b_3_c4), .C3(carrylookahead_logic_4b_3_c3),
    .C2(carrylookahead_logic_4b_3_c2), .C1(carrylookahead_logic_4b_3_c1));
  Full_Adder full_adder_10 (.A(A[22]), .B(B[22]), .Cin(carrylookahead_logic_4b_3_c2), .S(S[22]));  // open: Cout
  Full_Adder full_adder_11 (.A(A[21]), .B(B[21]), .Cin(carrylookahead_logic_4b_3_c1), .S(S[21]));  // open: Cout
  Full_Adder full_adder_12 (.A(A[20]), .B(B[20]), .Cin(carrylookahead_logic_4b_4_c4), .S(S[20]));  // open: Cout
  Full_Adder full_adder_13 (.A(A[19]), .B(B[19]), .Cin(carrylookahead_logic_4b_4_c3), .S(S[19]));  // open: Cout
  CarryLookAhead_logic_4b carrylookahead_logic_4b_4 (
    .A3(A[19]), .B3(B[19]), .A2(A[18]), .B2(B[18]), .A1(A[17]), .B1(B[17]), .A0(A[16]), .B0(B[16]),
    .Cin(carrylookahead_logic_4b_5_c4), .C4(carrylookahead_logic_4b_4_c4), .C3(carrylookahead_logic_4b_4_c3),
    .C2(carrylookahead_logic_4b_4_c2), .C1(carrylookahead_logic_4b_4_c1));
  Full_Adder full_adder_14 (.A(A[17]), .B(B[17]), .Cin(carrylookahead_logic_4b_4_c1), .S(S[17]));  // open: Cout
  Full_Adder full_adder_15 (.A(A[18]), .B(B[18]), .Cin(carrylookahead_logic_4b_4_c2), .S(S[18]));  // open: Cout
  Full_Adder full_adder_16 (.A(A[16]), .B(B[16]), .Cin(carrylookahead_logic_4b_5_c4), .S(S[16]));  // open: Cout
  Full_Adder full_adder_17 (.A(A[15]), .B(B[15]), .Cin(carrylookahead_logic_4b_5_c3), .S(S[15]));  // open: Cout
  CarryLookAhead_logic_4b carrylookahead_logic_4b_5 (
    .A3(A[15]), .B3(B[15]), .A2(A[14]), .B2(B[14]), .A1(A[13]), .B1(B[13]), .A0(A[12]), .B0(B[12]),
    .Cin(carrylookahead_logic_4b_6_c4), .C4(carrylookahead_logic_4b_5_c4), .C3(carrylookahead_logic_4b_5_c3),
    .C2(carrylookahead_logic_4b_5_c2), .C1(carrylookahead_logic_4b_5_c1));
  Full_Adder full_adder_18 (.A(A[14]), .B(B[14]), .Cin(carrylookahead_logic_4b_5_c2), .S(S[14]));  // open: Cout
  Full_Adder full_adder_19 (.A(A[13]), .B(B[13]), .Cin(carrylookahead_logic_4b_5_c1), .S(S[13]));  // open: Cout
  Full_Adder full_adder_20 (.A(A[12]), .B(B[12]), .Cin(carrylookahead_logic_4b_6_c4), .S(S[12]));  // open: Cout
  Full_Adder full_adder_21 (.A(A[11]), .B(B[11]), .Cin(carrylookahead_logic_4b_6_c3), .S(S[11]));  // open: Cout
  CarryLookAhead_logic_4b carrylookahead_logic_4b_6 (
    .A3(A[11]), .B3(B[11]), .A2(A[10]), .B2(B[10]), .A1(A[9]), .B1(B[9]), .A0(A[8]), .B0(B[8]),
    .Cin(carrylookahead_logic_4b_7_c4), .C4(carrylookahead_logic_4b_6_c4), .C3(carrylookahead_logic_4b_6_c3),
    .C2(carrylookahead_logic_4b_6_c2), .C1(carrylookahead_logic_4b_6_c1));
  Full_Adder full_adder_22 (.A(A[10]), .B(B[10]), .Cin(carrylookahead_logic_4b_6_c2), .S(S[10]));  // open: Cout
  Full_Adder full_adder_23 (.A(A[9]), .B(B[9]), .Cin(carrylookahead_logic_4b_6_c1), .S(S[9]));  // open: Cout
  Full_Adder full_adder_24 (.A(A[8]), .B(B[8]), .Cin(carrylookahead_logic_4b_7_c4), .S(S[8]));  // open: Cout
  Full_Adder full_adder_25 (.A(A[7]), .B(B[7]), .Cin(carrylookahead_logic_4b_7_c3), .S(S[7]));  // open: Cout
  CarryLookAhead_logic_4b carrylookahead_logic_4b_7 (
    .A3(A[7]), .B3(B[7]), .A2(A[6]), .B2(B[6]), .A1(A[5]), .B1(B[5]), .A0(A[4]), .B0(B[4]),
    .Cin(carrylookahead_logic_4b_8_c4), .C4(carrylookahead_logic_4b_7_c4), .C3(carrylookahead_logic_4b_7_c3),
    .C2(carrylookahead_logic_4b_7_c2), .C1(carrylookahead_logic_4b_7_c1));
  Full_Adder full_adder_26 (.A(A[6]), .B(B[6]), .Cin(carrylookahead_logic_4b_7_c2), .S(S[6]));  // open: Cout
  Full_Adder full_adder_27 (.A(A[5]), .B(B[5]), .Cin(carrylookahead_logic_4b_7_c1), .S(S[5]));  // open: Cout
  Full_Adder full_adder_28 (.A(A[4]), .B(B[4]), .Cin(carrylookahead_logic_4b_8_c4), .S(S[4]));  // open: Cout
  Full_Adder full_adder_29 (.A(A[3]), .B(B[3]), .Cin(carrylookahead_logic_4b_8_c3), .S(S[3]));  // open: Cout
  CarryLookAhead_logic_4b carrylookahead_logic_4b_8 (
    .A3(A[3]), .B3(B[3]), .A2(A[2]), .B2(B[2]), .A1(A[1]), .B1(B[1]), .A0(A[0]), .B0(B[0]), .Cin(Cin),
    .C4(carrylookahead_logic_4b_8_c4), .C3(carrylookahead_logic_4b_8_c3), .C2(carrylookahead_logic_4b_8_c2),
    .C1(carrylookahead_logic_4b_8_c1));
  Full_Adder full_adder_30 (.A(A[2]), .B(B[2]), .Cin(carrylookahead_logic_4b_8_c2), .S(S[2]));  // open: Cout
  Full_Adder full_adder_31 (.A(A[1]), .B(B[1]), .Cin(carrylookahead_logic_4b_8_c1), .S(S[1]));  // open: Cout
  Full_Adder full_adder_32 (.A(A[0]), .B(B[0]), .Cin(Cin), .S(S[0]));  // open: Cout
endmodule

// Lshifter32b
module Left_Shifter_32b (
  input  [31:0] A,
  input  [31:0] B,
  output [31:0] S
);

  wire multiplexer_1_out, multiplexer_2_out, multiplexer_3_out, multiplexer_4_out, multiplexer_5_out,
       multiplexer_6_out, multiplexer_7_out, multiplexer_8_out, multiplexer_9_out, multiplexer_10_out,
       multiplexer_11_out, multiplexer_12_out, multiplexer_13_out, multiplexer_14_out, multiplexer_15_out,
       multiplexer_16_out, multiplexer_17_out, multiplexer_18_out, multiplexer_19_out, multiplexer_20_out,
       multiplexer_21_out, multiplexer_22_out, multiplexer_23_out, multiplexer_24_out, multiplexer_25_out,
       multiplexer_26_out, multiplexer_27_out, multiplexer_28_out, multiplexer_29_out, multiplexer_30_out,
       multiplexer_31_out, multiplexer_32_out, multiplexer_33_out, multiplexer_34_out, multiplexer_35_out,
       multiplexer_36_out, multiplexer_37_out, multiplexer_38_out, multiplexer_39_out, multiplexer_40_out,
       multiplexer_41_out, multiplexer_42_out, multiplexer_43_out, multiplexer_44_out, multiplexer_45_out,
       multiplexer_46_out, multiplexer_47_out, multiplexer_48_out, multiplexer_49_out, multiplexer_50_out,
       multiplexer_51_out, multiplexer_52_out, multiplexer_53_out, multiplexer_54_out, multiplexer_55_out,
       multiplexer_56_out, multiplexer_57_out, multiplexer_58_out, multiplexer_59_out, multiplexer_60_out,
       multiplexer_61_out, multiplexer_62_out, multiplexer_63_out, multiplexer_64_out, multiplexer_65_out,
       multiplexer_66_out, multiplexer_67_out, multiplexer_68_out, multiplexer_69_out, multiplexer_70_out,
       multiplexer_71_out, multiplexer_72_out, multiplexer_73_out, multiplexer_74_out, multiplexer_75_out,
       multiplexer_76_out, multiplexer_77_out, multiplexer_78_out, multiplexer_79_out, multiplexer_80_out,
       multiplexer_81_out, multiplexer_82_out, multiplexer_83_out, multiplexer_84_out, multiplexer_85_out,
       multiplexer_86_out, multiplexer_87_out, multiplexer_88_out, multiplexer_89_out, multiplexer_90_out,
       multiplexer_91_out, multiplexer_92_out, multiplexer_93_out, multiplexer_94_out, multiplexer_95_out,
       multiplexer_96_out, multiplexer_97_out, multiplexer_98_out, multiplexer_99_out, multiplexer_100_out,
       multiplexer_101_out, multiplexer_102_out, multiplexer_103_out, multiplexer_104_out,
       multiplexer_105_out, multiplexer_106_out, multiplexer_107_out, multiplexer_108_out,
       multiplexer_109_out, multiplexer_110_out, multiplexer_111_out, multiplexer_112_out,
       multiplexer_113_out, multiplexer_114_out, multiplexer_115_out, multiplexer_116_out,
       multiplexer_117_out, multiplexer_118_out, multiplexer_119_out, multiplexer_120_out,
       multiplexer_121_out, multiplexer_122_out, multiplexer_123_out, multiplexer_124_out,
       multiplexer_125_out, multiplexer_126_out, multiplexer_127_out, multiplexer_128_out, or_1_out;
  wire [31:0] multiplexer_129_out;

  Multiplexer multiplexer_1 (.in0(A[0]), .in1(1'b0), .out(multiplexer_1_out), .sel(B[4]));
  Multiplexer multiplexer_2 (.in0(A[1]), .in1(1'b0), .out(multiplexer_2_out), .sel(B[4]));
  Multiplexer multiplexer_3 (.in0(A[2]), .in1(1'b0), .out(multiplexer_3_out), .sel(B[4]));
  Multiplexer multiplexer_4 (.in0(A[3]), .in1(1'b0), .out(multiplexer_4_out), .sel(B[4]));
  Multiplexer multiplexer_5 (.in0(A[4]), .in1(1'b0), .out(multiplexer_5_out), .sel(B[4]));
  Multiplexer multiplexer_6 (.in0(A[5]), .in1(1'b0), .out(multiplexer_6_out), .sel(B[4]));
  Multiplexer multiplexer_7 (.in0(A[6]), .in1(1'b0), .out(multiplexer_7_out), .sel(B[4]));
  Multiplexer multiplexer_8 (.in0(A[7]), .in1(1'b0), .out(multiplexer_8_out), .sel(B[4]));
  Multiplexer multiplexer_9 (.in0(A[8]), .in1(1'b0), .out(multiplexer_9_out), .sel(B[4]));
  Multiplexer multiplexer_10 (.in0(A[9]), .in1(1'b0), .out(multiplexer_10_out), .sel(B[4]));
  Multiplexer multiplexer_11 (.in0(A[10]), .in1(1'b0), .out(multiplexer_11_out), .sel(B[4]));
  Multiplexer multiplexer_12 (.in0(A[11]), .in1(1'b0), .out(multiplexer_12_out), .sel(B[4]));
  Multiplexer multiplexer_13 (.in0(A[12]), .in1(1'b0), .out(multiplexer_13_out), .sel(B[4]));
  Multiplexer multiplexer_14 (.in0(A[13]), .in1(1'b0), .out(multiplexer_14_out), .sel(B[4]));
  Multiplexer multiplexer_15 (.in0(A[14]), .in1(1'b0), .out(multiplexer_15_out), .sel(B[4]));
  Multiplexer multiplexer_16 (.in0(A[15]), .in1(1'b0), .out(multiplexer_16_out), .sel(B[4]));
  Multiplexer multiplexer_17 (.in0(A[16]), .in1(A[0]), .out(multiplexer_17_out), .sel(B[4]));
  Multiplexer multiplexer_18 (.in0(A[17]), .in1(A[1]), .out(multiplexer_18_out), .sel(B[4]));
  Multiplexer multiplexer_19 (.in0(A[18]), .in1(A[2]), .out(multiplexer_19_out), .sel(B[4]));
  Multiplexer multiplexer_20 (.in0(A[19]), .in1(A[3]), .out(multiplexer_20_out), .sel(B[4]));
  Multiplexer multiplexer_21 (.in0(A[20]), .in1(A[4]), .out(multiplexer_21_out), .sel(B[4]));
  Multiplexer multiplexer_22 (.in0(A[21]), .in1(A[5]), .out(multiplexer_22_out), .sel(B[4]));
  Multiplexer multiplexer_23 (.in0(A[22]), .in1(A[6]), .out(multiplexer_23_out), .sel(B[4]));
  Multiplexer multiplexer_24 (.in0(A[23]), .in1(A[7]), .out(multiplexer_24_out), .sel(B[4]));
  Multiplexer multiplexer_25 (.in0(A[24]), .in1(A[8]), .out(multiplexer_25_out), .sel(B[4]));
  Multiplexer multiplexer_26 (.in0(A[25]), .in1(A[9]), .out(multiplexer_26_out), .sel(B[4]));
  Multiplexer multiplexer_27 (.in0(A[26]), .in1(A[10]), .out(multiplexer_27_out), .sel(B[4]));
  Multiplexer multiplexer_28 (.in0(A[27]), .in1(A[11]), .out(multiplexer_28_out), .sel(B[4]));
  Multiplexer multiplexer_29 (.in0(A[28]), .in1(A[12]), .out(multiplexer_29_out), .sel(B[4]));
  Multiplexer multiplexer_30 (.in0(A[29]), .in1(A[13]), .out(multiplexer_30_out), .sel(B[4]));
  Multiplexer multiplexer_31 (.in0(A[30]), .in1(A[14]), .out(multiplexer_31_out), .sel(B[4]));
  Multiplexer multiplexer_32 (.in0(A[31]), .in1(A[16]), .out(multiplexer_32_out), .sel(B[4]));
  Multiplexer multiplexer_33 (.in0(multiplexer_1_out), .in1(1'b0), .out(multiplexer_33_out), .sel(B[3]));
  Multiplexer multiplexer_34 (.in0(multiplexer_2_out), .in1(1'b0), .out(multiplexer_34_out), .sel(B[3]));
  Multiplexer multiplexer_35 (.in0(multiplexer_3_out), .in1(1'b0), .out(multiplexer_35_out), .sel(B[3]));
  Multiplexer multiplexer_36 (.in0(multiplexer_4_out), .in1(1'b0), .out(multiplexer_36_out), .sel(B[3]));
  Multiplexer multiplexer_37 (.in0(multiplexer_5_out), .in1(1'b0), .out(multiplexer_37_out), .sel(B[3]));
  Multiplexer multiplexer_38 (.in0(multiplexer_6_out), .in1(1'b0), .out(multiplexer_38_out), .sel(B[3]));
  Multiplexer multiplexer_39 (.in0(multiplexer_7_out), .in1(1'b0), .out(multiplexer_39_out), .sel(B[3]));
  Multiplexer multiplexer_40 (.in0(multiplexer_8_out), .in1(1'b0), .out(multiplexer_40_out), .sel(B[3]));
  Multiplexer multiplexer_41 (.in0(multiplexer_9_out), .in1(multiplexer_1_out), .out(multiplexer_41_out), .sel(B[3]));
  Multiplexer multiplexer_42 (.in0(multiplexer_10_out), .in1(multiplexer_2_out), .out(multiplexer_42_out), .sel(B[3]));
  Multiplexer multiplexer_43 (.in0(multiplexer_11_out), .in1(multiplexer_3_out), .out(multiplexer_43_out), .sel(B[3]));
  Multiplexer multiplexer_44 (.in0(multiplexer_12_out), .in1(multiplexer_4_out), .out(multiplexer_44_out), .sel(B[3]));
  Multiplexer multiplexer_45 (.in0(multiplexer_13_out), .in1(multiplexer_5_out), .out(multiplexer_45_out), .sel(B[3]));
  Multiplexer multiplexer_46 (.in0(multiplexer_14_out), .in1(multiplexer_6_out), .out(multiplexer_46_out), .sel(B[3]));
  Multiplexer multiplexer_47 (.in0(multiplexer_15_out), .in1(multiplexer_7_out), .out(multiplexer_47_out), .sel(B[3]));
  Multiplexer multiplexer_48 (.in0(multiplexer_16_out), .in1(multiplexer_8_out), .out(multiplexer_48_out), .sel(B[3]));
  Multiplexer multiplexer_49 (.in0(multiplexer_17_out), .in1(multiplexer_9_out), .out(multiplexer_49_out), .sel(B[3]));
  Multiplexer multiplexer_50 (.in0(multiplexer_18_out), .in1(multiplexer_10_out), .out(multiplexer_50_out), .sel(B[3]));
  Multiplexer multiplexer_51 (.in0(multiplexer_19_out), .in1(multiplexer_11_out), .out(multiplexer_51_out), .sel(B[3]));
  Multiplexer multiplexer_52 (.in0(multiplexer_20_out), .in1(multiplexer_12_out), .out(multiplexer_52_out), .sel(B[3]));
  Multiplexer multiplexer_53 (.in0(multiplexer_21_out), .in1(multiplexer_13_out), .out(multiplexer_53_out), .sel(B[3]));
  Multiplexer multiplexer_54 (.in0(multiplexer_22_out), .in1(multiplexer_14_out), .out(multiplexer_54_out), .sel(B[3]));
  Multiplexer multiplexer_55 (.in0(multiplexer_23_out), .in1(multiplexer_15_out), .out(multiplexer_55_out), .sel(B[3]));
  Multiplexer multiplexer_56 (.in0(multiplexer_24_out), .in1(multiplexer_16_out), .out(multiplexer_56_out), .sel(B[3]));
  Multiplexer multiplexer_57 (.in0(multiplexer_25_out), .in1(multiplexer_17_out), .out(multiplexer_57_out), .sel(B[3]));
  Multiplexer multiplexer_58 (.in0(multiplexer_26_out), .in1(multiplexer_18_out), .out(multiplexer_58_out), .sel(B[3]));
  Multiplexer multiplexer_59 (.in0(multiplexer_27_out), .in1(multiplexer_19_out), .out(multiplexer_59_out), .sel(B[3]));
  Multiplexer multiplexer_60 (.in0(multiplexer_28_out), .in1(multiplexer_20_out), .out(multiplexer_60_out), .sel(B[3]));
  Multiplexer multiplexer_61 (.in0(multiplexer_29_out), .in1(multiplexer_21_out), .out(multiplexer_61_out), .sel(B[3]));
  Multiplexer multiplexer_62 (.in0(multiplexer_30_out), .in1(multiplexer_22_out), .out(multiplexer_62_out), .sel(B[3]));
  Multiplexer multiplexer_63 (.in0(multiplexer_31_out), .in1(multiplexer_23_out), .out(multiplexer_63_out), .sel(B[3]));
  Multiplexer multiplexer_64 (.in0(multiplexer_32_out), .in1(multiplexer_24_out), .out(multiplexer_64_out), .sel(B[3]));
  Multiplexer multiplexer_65 (.in0(multiplexer_33_out), .in1(1'b0), .out(multiplexer_65_out), .sel(B[2]));
  Multiplexer multiplexer_66 (.in0(multiplexer_34_out), .in1(1'b0), .out(multiplexer_66_out), .sel(B[2]));
  Multiplexer multiplexer_67 (.in0(multiplexer_35_out), .in1(1'b0), .out(multiplexer_67_out), .sel(B[2]));
  Multiplexer multiplexer_68 (.in0(multiplexer_36_out), .in1(1'b0), .out(multiplexer_68_out), .sel(B[2]));
  Multiplexer multiplexer_69 (.in0(multiplexer_37_out), .in1(multiplexer_33_out), .out(multiplexer_69_out), .sel(B[2]));
  Multiplexer multiplexer_70 (.in0(multiplexer_38_out), .in1(multiplexer_34_out), .out(multiplexer_70_out), .sel(B[2]));
  Multiplexer multiplexer_71 (.in0(multiplexer_39_out), .in1(multiplexer_35_out), .out(multiplexer_71_out), .sel(B[2]));
  Multiplexer multiplexer_72 (.in0(multiplexer_40_out), .in1(multiplexer_36_out), .out(multiplexer_72_out), .sel(B[2]));
  Multiplexer multiplexer_73 (.in0(multiplexer_41_out), .in1(multiplexer_37_out), .out(multiplexer_73_out), .sel(B[2]));
  Multiplexer multiplexer_74 (.in0(multiplexer_42_out), .in1(multiplexer_38_out), .out(multiplexer_74_out), .sel(B[2]));
  Multiplexer multiplexer_75 (.in0(multiplexer_43_out), .in1(multiplexer_39_out), .out(multiplexer_75_out), .sel(B[2]));
  Multiplexer multiplexer_76 (.in0(multiplexer_44_out), .in1(multiplexer_40_out), .out(multiplexer_76_out), .sel(B[2]));
  Multiplexer multiplexer_77 (.in0(multiplexer_45_out), .in1(multiplexer_41_out), .out(multiplexer_77_out), .sel(B[2]));
  Multiplexer multiplexer_78 (.in0(multiplexer_46_out), .in1(multiplexer_42_out), .out(multiplexer_78_out), .sel(B[2]));
  Multiplexer multiplexer_79 (.in0(multiplexer_47_out), .in1(multiplexer_43_out), .out(multiplexer_79_out), .sel(B[2]));
  Multiplexer multiplexer_80 (.in0(multiplexer_48_out), .in1(multiplexer_44_out), .out(multiplexer_80_out), .sel(B[2]));
  Multiplexer multiplexer_81 (.in0(multiplexer_49_out), .in1(multiplexer_45_out), .out(multiplexer_81_out), .sel(B[2]));
  Multiplexer multiplexer_82 (.in0(multiplexer_50_out), .in1(multiplexer_46_out), .out(multiplexer_82_out), .sel(B[2]));
  Multiplexer multiplexer_83 (.in0(multiplexer_51_out), .in1(multiplexer_47_out), .out(multiplexer_83_out), .sel(B[2]));
  Multiplexer multiplexer_84 (.in0(multiplexer_52_out), .in1(multiplexer_48_out), .out(multiplexer_84_out), .sel(B[2]));
  Multiplexer multiplexer_85 (.in0(multiplexer_53_out), .in1(multiplexer_49_out), .out(multiplexer_85_out), .sel(B[2]));
  Multiplexer multiplexer_86 (.in0(multiplexer_54_out), .in1(multiplexer_50_out), .out(multiplexer_86_out), .sel(B[2]));
  Multiplexer multiplexer_87 (.in0(multiplexer_55_out), .in1(multiplexer_51_out), .out(multiplexer_87_out), .sel(B[2]));
  Multiplexer multiplexer_88 (.in0(multiplexer_56_out), .in1(multiplexer_52_out), .out(multiplexer_88_out), .sel(B[2]));
  Multiplexer multiplexer_89 (.in0(multiplexer_57_out), .in1(multiplexer_53_out), .out(multiplexer_89_out), .sel(B[2]));
  Multiplexer multiplexer_90 (.in0(multiplexer_58_out), .in1(multiplexer_54_out), .out(multiplexer_90_out), .sel(B[2]));
  Multiplexer multiplexer_91 (.in0(multiplexer_59_out), .in1(multiplexer_55_out), .out(multiplexer_91_out), .sel(B[2]));
  Multiplexer multiplexer_92 (.in0(multiplexer_60_out), .in1(multiplexer_56_out), .out(multiplexer_92_out), .sel(B[2]));
  Multiplexer multiplexer_93 (.in0(multiplexer_61_out), .in1(multiplexer_57_out), .out(multiplexer_93_out), .sel(B[2]));
  Multiplexer multiplexer_94 (.in0(multiplexer_62_out), .in1(multiplexer_58_out), .out(multiplexer_94_out), .sel(B[2]));
  Multiplexer multiplexer_95 (.in0(multiplexer_63_out), .in1(multiplexer_59_out), .out(multiplexer_95_out), .sel(B[2]));
  Multiplexer multiplexer_96 (.in0(multiplexer_64_out), .in1(multiplexer_60_out), .out(multiplexer_96_out), .sel(B[2]));
  Multiplexer multiplexer_97 (.in0(multiplexer_65_out), .in1(1'b0), .out(multiplexer_97_out), .sel(B[1]));
  Multiplexer multiplexer_98 (.in0(multiplexer_66_out), .in1(1'b0), .out(multiplexer_98_out), .sel(B[1]));
  Multiplexer multiplexer_99 (.in0(multiplexer_67_out), .in1(multiplexer_65_out), .out(multiplexer_99_out), .sel(B[1]));
  Multiplexer multiplexer_100 (
    .in0(multiplexer_68_out), .in1(multiplexer_66_out), .out(multiplexer_100_out), .sel(B[1]));
  Multiplexer multiplexer_101 (
    .in0(multiplexer_69_out), .in1(multiplexer_67_out), .out(multiplexer_101_out), .sel(B[1]));
  Multiplexer multiplexer_102 (
    .in0(multiplexer_70_out), .in1(multiplexer_68_out), .out(multiplexer_102_out), .sel(B[1]));
  Multiplexer multiplexer_103 (
    .in0(multiplexer_71_out), .in1(multiplexer_69_out), .out(multiplexer_103_out), .sel(B[1]));
  Multiplexer multiplexer_104 (
    .in0(multiplexer_72_out), .in1(multiplexer_70_out), .out(multiplexer_104_out), .sel(B[1]));
  Multiplexer multiplexer_105 (
    .in0(multiplexer_73_out), .in1(multiplexer_71_out), .out(multiplexer_105_out), .sel(B[1]));
  Multiplexer multiplexer_106 (
    .in0(multiplexer_74_out), .in1(multiplexer_72_out), .out(multiplexer_106_out), .sel(B[1]));
  Multiplexer multiplexer_107 (
    .in0(multiplexer_75_out), .in1(multiplexer_73_out), .out(multiplexer_107_out), .sel(B[1]));
  Multiplexer multiplexer_108 (
    .in0(multiplexer_76_out), .in1(multiplexer_74_out), .out(multiplexer_108_out), .sel(B[1]));
  Multiplexer multiplexer_109 (
    .in0(multiplexer_77_out), .in1(multiplexer_75_out), .out(multiplexer_109_out), .sel(B[1]));
  Multiplexer multiplexer_110 (
    .in0(multiplexer_78_out), .in1(multiplexer_76_out), .out(multiplexer_110_out), .sel(B[1]));
  Multiplexer multiplexer_111 (
    .in0(multiplexer_79_out), .in1(multiplexer_77_out), .out(multiplexer_111_out), .sel(B[1]));
  Multiplexer multiplexer_112 (
    .in0(multiplexer_80_out), .in1(multiplexer_78_out), .out(multiplexer_112_out), .sel(B[1]));
  Multiplexer multiplexer_113 (
    .in0(multiplexer_81_out), .in1(multiplexer_79_out), .out(multiplexer_113_out), .sel(B[1]));
  Multiplexer multiplexer_114 (
    .in0(multiplexer_82_out), .in1(multiplexer_80_out), .out(multiplexer_114_out), .sel(B[1]));
  Multiplexer multiplexer_115 (
    .in0(multiplexer_83_out), .in1(multiplexer_81_out), .out(multiplexer_115_out), .sel(B[1]));
  Multiplexer multiplexer_116 (
    .in0(multiplexer_84_out), .in1(multiplexer_82_out), .out(multiplexer_116_out), .sel(B[1]));
  Multiplexer multiplexer_117 (
    .in0(multiplexer_85_out), .in1(multiplexer_83_out), .out(multiplexer_117_out), .sel(B[1]));
  Multiplexer multiplexer_118 (
    .in0(multiplexer_86_out), .in1(multiplexer_84_out), .out(multiplexer_118_out), .sel(B[1]));
  Multiplexer multiplexer_119 (
    .in0(multiplexer_87_out), .in1(multiplexer_85_out), .out(multiplexer_119_out), .sel(B[1]));
  Multiplexer multiplexer_120 (
    .in0(multiplexer_88_out), .in1(multiplexer_86_out), .out(multiplexer_120_out), .sel(B[1]));
  Multiplexer multiplexer_121 (
    .in0(multiplexer_89_out), .in1(multiplexer_87_out), .out(multiplexer_121_out), .sel(B[1]));
  Multiplexer multiplexer_122 (
    .in0(multiplexer_90_out), .in1(multiplexer_88_out), .out(multiplexer_122_out), .sel(B[1]));
  Multiplexer multiplexer_123 (
    .in0(multiplexer_91_out), .in1(multiplexer_89_out), .out(multiplexer_123_out), .sel(B[1]));
  Multiplexer multiplexer_124 (
    .in0(multiplexer_92_out), .in1(multiplexer_90_out), .out(multiplexer_124_out), .sel(B[1]));
  Multiplexer multiplexer_125 (
    .in0(multiplexer_93_out), .in1(multiplexer_91_out), .out(multiplexer_125_out), .sel(B[1]));
  Multiplexer multiplexer_126 (
    .in0(multiplexer_94_out), .in1(multiplexer_92_out), .out(multiplexer_126_out), .sel(B[1]));
  Multiplexer multiplexer_127 (
    .in0(multiplexer_95_out), .in1(multiplexer_93_out), .out(multiplexer_127_out), .sel(B[1]));
  Multiplexer multiplexer_128 (
    .in0(multiplexer_96_out), .in1(multiplexer_94_out), .out(multiplexer_128_out), .sel(B[1]));
  or or_1 (or_1_out, B[31], B[30], B[29], B[28], B[27], B[26], B[25], B[24], B[23], B[22], B[21], B[20], B[19], B[18], B[17], B[16], B[15], B[14], B[13], B[12], B[11], B[10], B[9], B[8], B[7], B[6], B[5]);
  Multiplexer multiplexer_129 (.in0(multiplexer_97_out), .in1(1'b0), .out(multiplexer_129_out[0]), .sel(B[0]));
  Multiplexer multiplexer_130 (
    .in0(multiplexer_98_out), .in1(multiplexer_97_out), .out(multiplexer_129_out[1]), .sel(B[0]));
  Multiplexer multiplexer_131 (
    .in0(multiplexer_99_out), .in1(multiplexer_98_out), .out(multiplexer_129_out[2]), .sel(B[0]));
  Multiplexer multiplexer_132 (
    .in0(multiplexer_100_out), .in1(multiplexer_99_out), .out(multiplexer_129_out[3]), .sel(B[0]));
  Multiplexer multiplexer_133 (
    .in0(multiplexer_101_out), .in1(multiplexer_100_out), .out(multiplexer_129_out[4]), .sel(B[0]));
  Multiplexer multiplexer_134 (
    .in0(multiplexer_102_out), .in1(multiplexer_101_out), .out(multiplexer_129_out[5]), .sel(B[0]));
  Multiplexer multiplexer_135 (
    .in0(multiplexer_103_out), .in1(multiplexer_102_out), .out(multiplexer_129_out[6]), .sel(B[0]));
  Multiplexer multiplexer_136 (
    .in0(multiplexer_104_out), .in1(multiplexer_103_out), .out(multiplexer_129_out[7]), .sel(B[0]));
  Multiplexer multiplexer_137 (
    .in0(multiplexer_105_out), .in1(multiplexer_104_out), .out(multiplexer_129_out[8]), .sel(B[0]));
  Multiplexer multiplexer_138 (
    .in0(multiplexer_106_out), .in1(multiplexer_105_out), .out(multiplexer_129_out[9]), .sel(B[0]));
  Multiplexer multiplexer_139 (
    .in0(multiplexer_107_out), .in1(multiplexer_106_out), .out(multiplexer_129_out[10]), .sel(B[0]));
  Multiplexer multiplexer_140 (
    .in0(multiplexer_108_out), .in1(multiplexer_107_out), .out(multiplexer_129_out[11]), .sel(B[0]));
  Multiplexer multiplexer_141 (
    .in0(multiplexer_109_out), .in1(multiplexer_108_out), .out(multiplexer_129_out[12]), .sel(B[0]));
  Multiplexer multiplexer_142 (
    .in0(multiplexer_110_out), .in1(multiplexer_109_out), .out(multiplexer_129_out[13]), .sel(B[0]));
  Multiplexer multiplexer_143 (
    .in0(multiplexer_111_out), .in1(multiplexer_110_out), .out(multiplexer_129_out[14]), .sel(B[0]));
  Multiplexer multiplexer_144 (
    .in0(multiplexer_112_out), .in1(multiplexer_111_out), .out(multiplexer_129_out[15]), .sel(B[0]));
  Multiplexer multiplexer_145 (
    .in0(multiplexer_113_out), .in1(multiplexer_112_out), .out(multiplexer_129_out[16]), .sel(B[0]));
  Multiplexer multiplexer_146 (
    .in0(multiplexer_114_out), .in1(multiplexer_113_out), .out(multiplexer_129_out[17]), .sel(B[0]));
  Multiplexer multiplexer_147 (
    .in0(multiplexer_115_out), .in1(multiplexer_114_out), .out(multiplexer_129_out[18]), .sel(B[0]));
  Multiplexer multiplexer_148 (
    .in0(multiplexer_116_out), .in1(multiplexer_115_out), .out(multiplexer_129_out[19]), .sel(B[0]));
  Multiplexer multiplexer_149 (
    .in0(multiplexer_117_out), .in1(multiplexer_116_out), .out(multiplexer_129_out[20]), .sel(B[0]));
  Multiplexer multiplexer_150 (
    .in0(multiplexer_118_out), .in1(multiplexer_117_out), .out(multiplexer_129_out[21]), .sel(B[0]));
  Multiplexer multiplexer_151 (
    .in0(multiplexer_119_out), .in1(multiplexer_118_out), .out(multiplexer_129_out[22]), .sel(B[0]));
  Multiplexer multiplexer_152 (
    .in0(multiplexer_120_out), .in1(multiplexer_119_out), .out(multiplexer_129_out[23]), .sel(B[0]));
  Multiplexer multiplexer_153 (
    .in0(multiplexer_121_out), .in1(multiplexer_120_out), .out(multiplexer_129_out[24]), .sel(B[0]));
  Multiplexer multiplexer_154 (
    .in0(multiplexer_122_out), .in1(multiplexer_121_out), .out(multiplexer_129_out[25]), .sel(B[0]));
  Multiplexer multiplexer_155 (
    .in0(multiplexer_123_out), .in1(multiplexer_122_out), .out(multiplexer_129_out[26]), .sel(B[0]));
  Multiplexer multiplexer_156 (
    .in0(multiplexer_124_out), .in1(multiplexer_123_out), .out(multiplexer_129_out[27]), .sel(B[0]));
  Multiplexer multiplexer_157 (
    .in0(multiplexer_125_out), .in1(multiplexer_124_out), .out(multiplexer_129_out[28]), .sel(B[0]));
  Multiplexer multiplexer_158 (
    .in0(multiplexer_126_out), .in1(multiplexer_125_out), .out(multiplexer_129_out[29]), .sel(B[0]));
  Multiplexer multiplexer_159 (
    .in0(multiplexer_127_out), .in1(multiplexer_126_out), .out(multiplexer_129_out[30]), .sel(B[0]));
  Multiplexer multiplexer_160 (
    .in0(multiplexer_128_out), .in1(multiplexer_127_out), .out(multiplexer_129_out[31]), .sel(B[0]));
  Multiplexer #(.width(32)) multiplexer_161 (.in0(multiplexer_129_out), .in1({32{1'b0}}), .out(S), .sel(or_1_out));
endmodule

// Rshifter32b
module Right_Shifter_32b (
  input  [31:0] A,
  input  [31:0] B,
  output [31:0] S
);

  wire multiplexer_1_out, multiplexer_2_out, multiplexer_3_out, multiplexer_4_out, multiplexer_5_out,
       multiplexer_6_out, multiplexer_7_out, multiplexer_8_out, multiplexer_9_out, multiplexer_10_out,
       multiplexer_11_out, multiplexer_12_out, multiplexer_13_out, multiplexer_14_out, multiplexer_15_out,
       multiplexer_16_out, multiplexer_17_out, multiplexer_18_out, multiplexer_19_out, multiplexer_20_out,
       multiplexer_21_out, multiplexer_22_out, multiplexer_23_out, multiplexer_24_out, multiplexer_25_out,
       multiplexer_26_out, multiplexer_27_out, multiplexer_28_out, multiplexer_29_out, multiplexer_30_out,
       multiplexer_31_out, multiplexer_32_out, multiplexer_33_out, multiplexer_34_out, multiplexer_35_out,
       multiplexer_36_out, multiplexer_37_out, multiplexer_38_out, multiplexer_39_out, multiplexer_40_out,
       multiplexer_41_out, multiplexer_42_out, multiplexer_43_out, multiplexer_44_out, multiplexer_45_out,
       multiplexer_46_out, multiplexer_47_out, multiplexer_48_out, multiplexer_49_out, multiplexer_50_out,
       multiplexer_51_out, multiplexer_52_out, multiplexer_53_out, multiplexer_54_out, multiplexer_55_out,
       multiplexer_56_out, multiplexer_57_out, multiplexer_58_out, multiplexer_59_out, multiplexer_60_out,
       multiplexer_61_out, multiplexer_62_out, multiplexer_63_out, multiplexer_64_out, multiplexer_65_out,
       multiplexer_66_out, multiplexer_67_out, multiplexer_68_out, multiplexer_69_out, multiplexer_70_out,
       multiplexer_71_out, multiplexer_72_out, multiplexer_73_out, multiplexer_74_out, multiplexer_75_out,
       multiplexer_76_out, multiplexer_77_out, multiplexer_78_out, multiplexer_79_out, multiplexer_80_out,
       multiplexer_81_out, multiplexer_82_out, multiplexer_83_out, multiplexer_84_out, multiplexer_85_out,
       multiplexer_86_out, multiplexer_87_out, multiplexer_88_out, multiplexer_89_out, multiplexer_90_out,
       multiplexer_91_out, multiplexer_92_out, multiplexer_93_out, multiplexer_94_out, multiplexer_95_out,
       multiplexer_96_out, multiplexer_97_out, multiplexer_98_out, multiplexer_99_out, multiplexer_100_out,
       multiplexer_101_out, multiplexer_102_out, multiplexer_103_out, multiplexer_104_out,
       multiplexer_105_out, multiplexer_106_out, multiplexer_107_out, multiplexer_108_out,
       multiplexer_109_out, multiplexer_110_out, multiplexer_111_out, multiplexer_112_out,
       multiplexer_113_out, multiplexer_114_out, multiplexer_115_out, multiplexer_116_out,
       multiplexer_117_out, multiplexer_118_out, multiplexer_119_out, multiplexer_120_out,
       multiplexer_121_out, multiplexer_122_out, multiplexer_123_out, multiplexer_124_out,
       multiplexer_125_out, multiplexer_126_out, multiplexer_127_out, multiplexer_128_out, or_1_out;
  wire [31:0] multiplexer_129_out;

  Multiplexer multiplexer_1 (.in0(A[0]), .in1(A[15]), .out(multiplexer_1_out), .sel(B[4]));
  Multiplexer multiplexer_2 (.in0(A[1]), .in1(A[16]), .out(multiplexer_2_out), .sel(B[4]));
  Multiplexer multiplexer_3 (.in0(A[2]), .in1(A[18]), .out(multiplexer_3_out), .sel(B[4]));
  Multiplexer multiplexer_4 (.in0(A[3]), .in1(A[19]), .out(multiplexer_4_out), .sel(B[4]));
  Multiplexer multiplexer_5 (.in0(A[4]), .in1(A[20]), .out(multiplexer_5_out), .sel(B[4]));
  Multiplexer multiplexer_6 (.in0(A[5]), .in1(A[21]), .out(multiplexer_6_out), .sel(B[4]));
  Multiplexer multiplexer_7 (.in0(A[6]), .in1(A[22]), .out(multiplexer_7_out), .sel(B[4]));
  Multiplexer multiplexer_8 (.in0(A[7]), .in1(A[23]), .out(multiplexer_8_out), .sel(B[4]));
  Multiplexer multiplexer_9 (.in0(A[8]), .in1(A[24]), .out(multiplexer_9_out), .sel(B[4]));
  Multiplexer multiplexer_10 (.in0(A[9]), .in1(A[25]), .out(multiplexer_10_out), .sel(B[4]));
  Multiplexer multiplexer_11 (.in0(A[10]), .in1(A[26]), .out(multiplexer_11_out), .sel(B[4]));
  Multiplexer multiplexer_12 (.in0(A[11]), .in1(A[27]), .out(multiplexer_12_out), .sel(B[4]));
  Multiplexer multiplexer_13 (.in0(A[12]), .in1(A[28]), .out(multiplexer_13_out), .sel(B[4]));
  Multiplexer multiplexer_14 (.in0(A[13]), .in1(A[29]), .out(multiplexer_14_out), .sel(B[4]));
  Multiplexer multiplexer_15 (.in0(A[14]), .in1(A[30]), .out(multiplexer_15_out), .sel(B[4]));
  Multiplexer multiplexer_16 (.in0(A[15]), .in1(A[31]), .out(multiplexer_16_out), .sel(B[4]));
  Multiplexer multiplexer_17 (.in0(A[16]), .in1(1'b0), .out(multiplexer_17_out), .sel(B[4]));
  Multiplexer multiplexer_18 (.in0(A[17]), .in1(1'b0), .out(multiplexer_18_out), .sel(B[4]));
  Multiplexer multiplexer_19 (.in0(A[18]), .in1(1'b0), .out(multiplexer_19_out), .sel(B[4]));
  Multiplexer multiplexer_20 (.in0(A[19]), .in1(1'b0), .out(multiplexer_20_out), .sel(B[4]));
  Multiplexer multiplexer_21 (.in0(A[20]), .in1(1'b0), .out(multiplexer_21_out), .sel(B[4]));
  Multiplexer multiplexer_22 (.in0(A[21]), .in1(1'b0), .out(multiplexer_22_out), .sel(B[4]));
  Multiplexer multiplexer_23 (.in0(A[22]), .in1(1'b0), .out(multiplexer_23_out), .sel(B[4]));
  Multiplexer multiplexer_24 (.in0(A[23]), .in1(1'b0), .out(multiplexer_24_out), .sel(B[4]));
  Multiplexer multiplexer_25 (.in0(A[24]), .in1(1'b0), .out(multiplexer_25_out), .sel(B[4]));
  Multiplexer multiplexer_26 (.in0(A[25]), .in1(1'b0), .out(multiplexer_26_out), .sel(B[4]));
  Multiplexer multiplexer_27 (.in0(A[26]), .in1(1'b0), .out(multiplexer_27_out), .sel(B[4]));
  Multiplexer multiplexer_28 (.in0(A[27]), .in1(1'b0), .out(multiplexer_28_out), .sel(B[4]));
  Multiplexer multiplexer_29 (.in0(A[28]), .in1(1'b0), .out(multiplexer_29_out), .sel(B[4]));
  Multiplexer multiplexer_30 (.in0(A[29]), .in1(1'b0), .out(multiplexer_30_out), .sel(B[4]));
  Multiplexer multiplexer_31 (.in0(A[30]), .in1(1'b0), .out(multiplexer_31_out), .sel(B[4]));
  Multiplexer multiplexer_32 (.in0(A[31]), .in1(1'b0), .out(multiplexer_32_out), .sel(B[4]));
  Multiplexer multiplexer_33 (.in0(multiplexer_1_out), .in1(multiplexer_9_out), .out(multiplexer_33_out), .sel(B[3]));
  Multiplexer multiplexer_34 (.in0(multiplexer_2_out), .in1(multiplexer_10_out), .out(multiplexer_34_out), .sel(B[3]));
  Multiplexer multiplexer_35 (.in0(multiplexer_3_out), .in1(multiplexer_11_out), .out(multiplexer_35_out), .sel(B[3]));
  Multiplexer multiplexer_36 (.in0(multiplexer_4_out), .in1(multiplexer_12_out), .out(multiplexer_36_out), .sel(B[3]));
  Multiplexer multiplexer_37 (.in0(multiplexer_5_out), .in1(multiplexer_13_out), .out(multiplexer_37_out), .sel(B[3]));
  Multiplexer multiplexer_38 (.in0(multiplexer_6_out), .in1(multiplexer_14_out), .out(multiplexer_38_out), .sel(B[3]));
  Multiplexer multiplexer_39 (.in0(multiplexer_7_out), .in1(multiplexer_15_out), .out(multiplexer_39_out), .sel(B[3]));
  Multiplexer multiplexer_40 (.in0(multiplexer_8_out), .in1(multiplexer_16_out), .out(multiplexer_40_out), .sel(B[3]));
  Multiplexer multiplexer_41 (.in0(multiplexer_9_out), .in1(multiplexer_17_out), .out(multiplexer_41_out), .sel(B[3]));
  Multiplexer multiplexer_42 (.in0(multiplexer_10_out), .in1(multiplexer_18_out), .out(multiplexer_42_out), .sel(B[3]));
  Multiplexer multiplexer_43 (.in0(multiplexer_11_out), .in1(multiplexer_19_out), .out(multiplexer_43_out), .sel(B[3]));
  Multiplexer multiplexer_44 (.in0(multiplexer_12_out), .in1(multiplexer_20_out), .out(multiplexer_44_out), .sel(B[3]));
  Multiplexer multiplexer_45 (.in0(multiplexer_13_out), .in1(multiplexer_21_out), .out(multiplexer_45_out), .sel(B[3]));
  Multiplexer multiplexer_46 (.in0(multiplexer_14_out), .in1(multiplexer_22_out), .out(multiplexer_46_out), .sel(B[3]));
  Multiplexer multiplexer_47 (.in0(multiplexer_15_out), .in1(multiplexer_23_out), .out(multiplexer_47_out), .sel(B[3]));
  Multiplexer multiplexer_48 (.in0(multiplexer_16_out), .in1(multiplexer_24_out), .out(multiplexer_48_out), .sel(B[3]));
  Multiplexer multiplexer_49 (.in0(multiplexer_17_out), .in1(multiplexer_25_out), .out(multiplexer_49_out), .sel(B[3]));
  Multiplexer multiplexer_50 (.in0(multiplexer_18_out), .in1(multiplexer_26_out), .out(multiplexer_50_out), .sel(B[3]));
  Multiplexer multiplexer_51 (.in0(multiplexer_19_out), .in1(multiplexer_27_out), .out(multiplexer_51_out), .sel(B[3]));
  Multiplexer multiplexer_52 (.in0(multiplexer_20_out), .in1(multiplexer_28_out), .out(multiplexer_52_out), .sel(B[3]));
  Multiplexer multiplexer_53 (.in0(multiplexer_21_out), .in1(multiplexer_29_out), .out(multiplexer_53_out), .sel(B[3]));
  Multiplexer multiplexer_54 (.in0(multiplexer_22_out), .in1(multiplexer_30_out), .out(multiplexer_54_out), .sel(B[3]));
  Multiplexer multiplexer_55 (.in0(multiplexer_23_out), .in1(multiplexer_31_out), .out(multiplexer_55_out), .sel(B[3]));
  Multiplexer multiplexer_56 (.in0(multiplexer_24_out), .in1(multiplexer_32_out), .out(multiplexer_56_out), .sel(B[3]));
  Multiplexer multiplexer_57 (.in0(multiplexer_25_out), .in1(1'b0), .out(multiplexer_57_out), .sel(B[3]));
  Multiplexer multiplexer_58 (.in0(multiplexer_26_out), .in1(1'b0), .out(multiplexer_58_out), .sel(B[3]));
  Multiplexer multiplexer_59 (.in0(multiplexer_27_out), .in1(1'b0), .out(multiplexer_59_out), .sel(B[3]));
  Multiplexer multiplexer_60 (.in0(multiplexer_28_out), .in1(1'b0), .out(multiplexer_60_out), .sel(B[3]));
  Multiplexer multiplexer_61 (.in0(multiplexer_29_out), .in1(1'b0), .out(multiplexer_61_out), .sel(B[3]));
  Multiplexer multiplexer_62 (.in0(multiplexer_30_out), .in1(1'b0), .out(multiplexer_62_out), .sel(B[3]));
  Multiplexer multiplexer_63 (.in0(multiplexer_31_out), .in1(1'b0), .out(multiplexer_63_out), .sel(B[3]));
  Multiplexer multiplexer_64 (.in0(multiplexer_32_out), .in1(1'b0), .out(multiplexer_64_out), .sel(B[3]));
  Multiplexer multiplexer_65 (.in0(multiplexer_33_out), .in1(multiplexer_37_out), .out(multiplexer_65_out), .sel(B[2]));
  Multiplexer multiplexer_66 (.in0(multiplexer_34_out), .in1(multiplexer_38_out), .out(multiplexer_66_out), .sel(B[2]));
  Multiplexer multiplexer_67 (.in0(multiplexer_35_out), .in1(multiplexer_39_out), .out(multiplexer_67_out), .sel(B[2]));
  Multiplexer multiplexer_68 (.in0(multiplexer_36_out), .in1(multiplexer_40_out), .out(multiplexer_68_out), .sel(B[2]));
  Multiplexer multiplexer_69 (.in0(multiplexer_37_out), .in1(multiplexer_41_out), .out(multiplexer_69_out), .sel(B[2]));
  Multiplexer multiplexer_70 (.in0(multiplexer_38_out), .in1(multiplexer_42_out), .out(multiplexer_70_out), .sel(B[2]));
  Multiplexer multiplexer_71 (.in0(multiplexer_39_out), .in1(multiplexer_43_out), .out(multiplexer_71_out), .sel(B[2]));
  Multiplexer multiplexer_72 (.in0(multiplexer_40_out), .in1(multiplexer_44_out), .out(multiplexer_72_out), .sel(B[2]));
  Multiplexer multiplexer_73 (.in0(multiplexer_41_out), .in1(multiplexer_45_out), .out(multiplexer_73_out), .sel(B[2]));
  Multiplexer multiplexer_74 (.in0(multiplexer_42_out), .in1(multiplexer_46_out), .out(multiplexer_74_out), .sel(B[2]));
  Multiplexer multiplexer_75 (.in0(multiplexer_43_out), .in1(multiplexer_47_out), .out(multiplexer_75_out), .sel(B[2]));
  Multiplexer multiplexer_76 (.in0(multiplexer_44_out), .in1(multiplexer_48_out), .out(multiplexer_76_out), .sel(B[2]));
  Multiplexer multiplexer_77 (.in0(multiplexer_45_out), .in1(multiplexer_49_out), .out(multiplexer_77_out), .sel(B[2]));
  Multiplexer multiplexer_78 (.in0(multiplexer_46_out), .in1(multiplexer_50_out), .out(multiplexer_78_out), .sel(B[2]));
  Multiplexer multiplexer_79 (.in0(multiplexer_47_out), .in1(multiplexer_51_out), .out(multiplexer_79_out), .sel(B[2]));
  Multiplexer multiplexer_80 (.in0(multiplexer_48_out), .in1(multiplexer_52_out), .out(multiplexer_80_out), .sel(B[2]));
  Multiplexer multiplexer_81 (.in0(multiplexer_49_out), .in1(multiplexer_53_out), .out(multiplexer_81_out), .sel(B[2]));
  Multiplexer multiplexer_82 (.in0(multiplexer_50_out), .in1(multiplexer_54_out), .out(multiplexer_82_out), .sel(B[2]));
  Multiplexer multiplexer_83 (.in0(multiplexer_51_out), .in1(multiplexer_55_out), .out(multiplexer_83_out), .sel(B[2]));
  Multiplexer multiplexer_84 (.in0(multiplexer_52_out), .in1(multiplexer_56_out), .out(multiplexer_84_out), .sel(B[2]));
  Multiplexer multiplexer_85 (.in0(multiplexer_53_out), .in1(multiplexer_57_out), .out(multiplexer_85_out), .sel(B[2]));
  Multiplexer multiplexer_86 (.in0(multiplexer_54_out), .in1(multiplexer_58_out), .out(multiplexer_86_out), .sel(B[2]));
  Multiplexer multiplexer_87 (.in0(multiplexer_55_out), .in1(multiplexer_59_out), .out(multiplexer_87_out), .sel(B[2]));
  Multiplexer multiplexer_88 (.in0(multiplexer_56_out), .in1(multiplexer_60_out), .out(multiplexer_88_out), .sel(B[2]));
  Multiplexer multiplexer_89 (.in0(multiplexer_57_out), .in1(multiplexer_61_out), .out(multiplexer_89_out), .sel(B[2]));
  Multiplexer multiplexer_90 (.in0(multiplexer_58_out), .in1(multiplexer_62_out), .out(multiplexer_90_out), .sel(B[2]));
  Multiplexer multiplexer_91 (.in0(multiplexer_59_out), .in1(multiplexer_63_out), .out(multiplexer_91_out), .sel(B[2]));
  Multiplexer multiplexer_92 (.in0(multiplexer_60_out), .in1(multiplexer_64_out), .out(multiplexer_92_out), .sel(B[2]));
  Multiplexer multiplexer_93 (.in0(multiplexer_61_out), .in1(1'b0), .out(multiplexer_93_out), .sel(B[2]));
  Multiplexer multiplexer_94 (.in0(multiplexer_62_out), .in1(1'b0), .out(multiplexer_94_out), .sel(B[2]));
  Multiplexer multiplexer_95 (.in0(multiplexer_63_out), .in1(1'b0), .out(multiplexer_95_out), .sel(B[2]));
  Multiplexer multiplexer_96 (.in0(multiplexer_64_out), .in1(1'b0), .out(multiplexer_96_out), .sel(B[2]));
  Multiplexer multiplexer_97 (.in0(multiplexer_65_out), .in1(multiplexer_67_out), .out(multiplexer_97_out), .sel(B[1]));
  Multiplexer multiplexer_98 (.in0(multiplexer_66_out), .in1(multiplexer_68_out), .out(multiplexer_98_out), .sel(B[1]));
  Multiplexer multiplexer_99 (.in0(multiplexer_67_out), .in1(multiplexer_69_out), .out(multiplexer_99_out), .sel(B[1]));
  Multiplexer multiplexer_100 (
    .in0(multiplexer_68_out), .in1(multiplexer_70_out), .out(multiplexer_100_out), .sel(B[1]));
  Multiplexer multiplexer_101 (
    .in0(multiplexer_69_out), .in1(multiplexer_71_out), .out(multiplexer_101_out), .sel(B[1]));
  Multiplexer multiplexer_102 (
    .in0(multiplexer_70_out), .in1(multiplexer_72_out), .out(multiplexer_102_out), .sel(B[1]));
  Multiplexer multiplexer_103 (
    .in0(multiplexer_71_out), .in1(multiplexer_73_out), .out(multiplexer_103_out), .sel(B[1]));
  Multiplexer multiplexer_104 (
    .in0(multiplexer_72_out), .in1(multiplexer_74_out), .out(multiplexer_104_out), .sel(B[1]));
  Multiplexer multiplexer_105 (
    .in0(multiplexer_73_out), .in1(multiplexer_75_out), .out(multiplexer_105_out), .sel(B[1]));
  Multiplexer multiplexer_106 (
    .in0(multiplexer_74_out), .in1(multiplexer_76_out), .out(multiplexer_106_out), .sel(B[1]));
  Multiplexer multiplexer_107 (
    .in0(multiplexer_75_out), .in1(multiplexer_77_out), .out(multiplexer_107_out), .sel(B[1]));
  Multiplexer multiplexer_108 (
    .in0(multiplexer_76_out), .in1(multiplexer_78_out), .out(multiplexer_108_out), .sel(B[1]));
  Multiplexer multiplexer_109 (
    .in0(multiplexer_77_out), .in1(multiplexer_79_out), .out(multiplexer_109_out), .sel(B[1]));
  Multiplexer multiplexer_110 (
    .in0(multiplexer_78_out), .in1(multiplexer_80_out), .out(multiplexer_110_out), .sel(B[1]));
  Multiplexer multiplexer_111 (
    .in0(multiplexer_79_out), .in1(multiplexer_81_out), .out(multiplexer_111_out), .sel(B[1]));
  Multiplexer multiplexer_112 (
    .in0(multiplexer_80_out), .in1(multiplexer_82_out), .out(multiplexer_112_out), .sel(B[1]));
  Multiplexer multiplexer_113 (
    .in0(multiplexer_81_out), .in1(multiplexer_83_out), .out(multiplexer_113_out), .sel(B[1]));
  Multiplexer multiplexer_114 (
    .in0(multiplexer_82_out), .in1(multiplexer_84_out), .out(multiplexer_114_out), .sel(B[1]));
  Multiplexer multiplexer_115 (
    .in0(multiplexer_83_out), .in1(multiplexer_85_out), .out(multiplexer_115_out), .sel(B[1]));
  Multiplexer multiplexer_116 (
    .in0(multiplexer_84_out), .in1(multiplexer_86_out), .out(multiplexer_116_out), .sel(B[1]));
  Multiplexer multiplexer_117 (
    .in0(multiplexer_85_out), .in1(multiplexer_87_out), .out(multiplexer_117_out), .sel(B[1]));
  Multiplexer multiplexer_118 (
    .in0(multiplexer_86_out), .in1(multiplexer_88_out), .out(multiplexer_118_out), .sel(B[1]));
  Multiplexer multiplexer_119 (
    .in0(multiplexer_87_out), .in1(multiplexer_89_out), .out(multiplexer_119_out), .sel(B[1]));
  Multiplexer multiplexer_120 (
    .in0(multiplexer_88_out), .in1(multiplexer_90_out), .out(multiplexer_120_out), .sel(B[1]));
  Multiplexer multiplexer_121 (
    .in0(multiplexer_89_out), .in1(multiplexer_91_out), .out(multiplexer_121_out), .sel(B[1]));
  Multiplexer multiplexer_122 (
    .in0(multiplexer_90_out), .in1(multiplexer_92_out), .out(multiplexer_122_out), .sel(B[1]));
  Multiplexer multiplexer_123 (
    .in0(multiplexer_91_out), .in1(multiplexer_93_out), .out(multiplexer_123_out), .sel(B[1]));
  Multiplexer multiplexer_124 (
    .in0(multiplexer_92_out), .in1(multiplexer_94_out), .out(multiplexer_124_out), .sel(B[1]));
  Multiplexer multiplexer_125 (
    .in0(multiplexer_93_out), .in1(multiplexer_95_out), .out(multiplexer_125_out), .sel(B[1]));
  Multiplexer multiplexer_126 (
    .in0(multiplexer_94_out), .in1(multiplexer_96_out), .out(multiplexer_126_out), .sel(B[1]));
  Multiplexer multiplexer_127 (.in0(multiplexer_95_out), .in1(1'b0), .out(multiplexer_127_out), .sel(B[1]));
  Multiplexer multiplexer_128 (.in0(multiplexer_96_out), .in1(1'b0), .out(multiplexer_128_out), .sel(B[1]));
  or or_1 (or_1_out, B[31], B[30], B[29], B[28], B[27], B[26], B[25], B[24], B[23], B[22], B[21], B[20], B[19], B[18], B[17], B[16], B[15], B[14], B[13], B[12], B[11], B[10], B[9], B[8], B[7], B[6], B[5]);
  Multiplexer multiplexer_129 (
    .in0(multiplexer_97_out), .in1(multiplexer_98_out), .out(multiplexer_129_out[0]), .sel(B[0]));
  Multiplexer multiplexer_130 (
    .in0(multiplexer_98_out), .in1(multiplexer_99_out), .out(multiplexer_129_out[1]), .sel(B[0]));
  Multiplexer multiplexer_131 (
    .in0(multiplexer_99_out), .in1(multiplexer_100_out), .out(multiplexer_129_out[2]), .sel(B[0]));
  Multiplexer multiplexer_132 (
    .in0(multiplexer_100_out), .in1(multiplexer_101_out), .out(multiplexer_129_out[3]), .sel(B[0]));
  Multiplexer multiplexer_133 (
    .in0(multiplexer_101_out), .in1(multiplexer_102_out), .out(multiplexer_129_out[4]), .sel(B[0]));
  Multiplexer multiplexer_134 (
    .in0(multiplexer_102_out), .in1(multiplexer_103_out), .out(multiplexer_129_out[5]), .sel(B[0]));
  Multiplexer multiplexer_135 (
    .in0(multiplexer_103_out), .in1(multiplexer_104_out), .out(multiplexer_129_out[6]), .sel(B[0]));
  Multiplexer multiplexer_136 (
    .in0(multiplexer_104_out), .in1(multiplexer_105_out), .out(multiplexer_129_out[7]), .sel(B[0]));
  Multiplexer multiplexer_137 (
    .in0(multiplexer_105_out), .in1(multiplexer_106_out), .out(multiplexer_129_out[8]), .sel(B[0]));
  Multiplexer multiplexer_138 (
    .in0(multiplexer_106_out), .in1(multiplexer_107_out), .out(multiplexer_129_out[9]), .sel(B[0]));
  Multiplexer multiplexer_139 (
    .in0(multiplexer_107_out), .in1(multiplexer_108_out), .out(multiplexer_129_out[10]), .sel(B[0]));
  Multiplexer multiplexer_140 (
    .in0(multiplexer_108_out), .in1(multiplexer_109_out), .out(multiplexer_129_out[11]), .sel(B[0]));
  Multiplexer multiplexer_141 (
    .in0(multiplexer_109_out), .in1(multiplexer_110_out), .out(multiplexer_129_out[12]), .sel(B[0]));
  Multiplexer multiplexer_142 (
    .in0(multiplexer_110_out), .in1(multiplexer_111_out), .out(multiplexer_129_out[13]), .sel(B[0]));
  Multiplexer multiplexer_143 (
    .in0(multiplexer_111_out), .in1(multiplexer_112_out), .out(multiplexer_129_out[14]), .sel(B[0]));
  Multiplexer multiplexer_144 (
    .in0(multiplexer_112_out), .in1(multiplexer_113_out), .out(multiplexer_129_out[15]), .sel(B[0]));
  Multiplexer multiplexer_145 (
    .in0(multiplexer_113_out), .in1(multiplexer_114_out), .out(multiplexer_129_out[16]), .sel(B[0]));
  Multiplexer multiplexer_146 (
    .in0(multiplexer_114_out), .in1(multiplexer_115_out), .out(multiplexer_129_out[17]), .sel(B[0]));
  Multiplexer multiplexer_147 (
    .in0(multiplexer_115_out), .in1(multiplexer_116_out), .out(multiplexer_129_out[18]), .sel(B[0]));
  Multiplexer multiplexer_148 (
    .in0(multiplexer_116_out), .in1(multiplexer_117_out), .out(multiplexer_129_out[19]), .sel(B[0]));
  Multiplexer multiplexer_149 (
    .in0(multiplexer_117_out), .in1(multiplexer_118_out), .out(multiplexer_129_out[20]), .sel(B[0]));
  Multiplexer multiplexer_150 (
    .in0(multiplexer_118_out), .in1(multiplexer_119_out), .out(multiplexer_129_out[21]), .sel(B[0]));
  Multiplexer multiplexer_151 (
    .in0(multiplexer_119_out), .in1(multiplexer_120_out), .out(multiplexer_129_out[22]), .sel(B[0]));
  Multiplexer multiplexer_152 (
    .in0(multiplexer_120_out), .in1(multiplexer_121_out), .out(multiplexer_129_out[23]), .sel(B[0]));
  Multiplexer multiplexer_153 (
    .in0(multiplexer_121_out), .in1(multiplexer_122_out), .out(multiplexer_129_out[24]), .sel(B[0]));
  Multiplexer multiplexer_154 (
    .in0(multiplexer_122_out), .in1(multiplexer_123_out), .out(multiplexer_129_out[25]), .sel(B[0]));
  Multiplexer multiplexer_155 (
    .in0(multiplexer_123_out), .in1(multiplexer_124_out), .out(multiplexer_129_out[26]), .sel(B[0]));
  Multiplexer multiplexer_156 (
    .in0(multiplexer_124_out), .in1(multiplexer_125_out), .out(multiplexer_129_out[27]), .sel(B[0]));
  Multiplexer multiplexer_157 (
    .in0(multiplexer_125_out), .in1(multiplexer_126_out), .out(multiplexer_129_out[28]), .sel(B[0]));
  Multiplexer multiplexer_158 (
    .in0(multiplexer_126_out), .in1(multiplexer_127_out), .out(multiplexer_129_out[29]), .sel(B[0]));
  Multiplexer multiplexer_159 (
    .in0(multiplexer_127_out), .in1(multiplexer_128_out), .out(multiplexer_129_out[30]), .sel(B[0]));
  Multiplexer multiplexer_160 (.in0(multiplexer_128_out), .in1(1'b0), .out(multiplexer_129_out[31]), .sel(B[0]));
  Multiplexer #(.width(32)) multiplexer_161 (.in0(multiplexer_129_out), .in1({32{1'b0}}), .out(S), .sel(or_1_out));
endmodule

// CLAlogic4b
module CarryLookAhead_logic_4b (
  input  Cin,
  input  A2,
  input  B2,
  input  A1,
  input  B1,
  input  A0,
  input  B0,
  input  A3,
  input  B3,
  output C4,
  output C3,
  output C2,
  output C1
);

  wire and_1_out, and_2_out, and_3_out, and_4_out, and_5_out, and_6_out, and_7_out, and_8_out, and_9_out,
       and_10_out, G0_out, G1_out, G2_out, G3_out, P0_out, P1_out, P2_out, P3_out;

  and G3 (G3_out, A3, B3);
  xor P3 (P3_out, A3, B3);
  and and_1 (and_1_out, P3_out, G2_out);
  or or_1 (C4, G3_out, and_1_out, and_2_out, and_3_out, and_4_out);
  and and_2 (and_2_out, P3_out, P2_out, G1_out);
  and and_3 (and_3_out, P3_out, P2_out, P1_out, G0_out);
  and and_4 (and_4_out, P3_out, P2_out, P1_out, P0_out, Cin);
  and G2 (G2_out, A2, B2);
  or or_2 (C3, G2_out, and_5_out, and_6_out, and_7_out);
  xor P2 (P2_out, A2, B2);
  and and_5 (and_5_out, P2_out, G1_out);
  and and_6 (and_6_out, P2_out, P1_out, G0_out);
  and and_7 (and_7_out, P2_out, P1_out, P0_out, Cin);
  and G1 (G1_out, A1, B1);
  or or_3 (C2, G1_out, and_8_out, and_9_out);
  xor P1 (P1_out, A1, B1);
  and and_8 (and_8_out, P1_out, G0_out);
  and G0 (G0_out, A0, B0);
  and and_9 (and_9_out, Cin, P1_out, P0_out);
  xor P0 (P0_out, A0, B0);
  and and_10 (and_10_out, P0_out, Cin);
  or or_4 (C1, G0_out, and_10_out);
endmodule

// FA
module Full_Adder (
  input  A,
  input  B,
  input  Cin,
  output Cout,
  output S
);

  wire and_1_out, and_2_out, or_2_out, xor_1_out;

  or or_1 (Cout, and_1_out, and_2_out);
  and and_1 (and_1_out, A, B);
  and and_2 (and_2_out, Cin, or_2_out);
  or or_2 (or_2_out, A, B);
  xor xor_1 (xor_1_out, A, B);
  xor xor_2 (S, xor_1_out, Cin);
endmodule
